// Logisim project project.circ as structural Verilog: 18 circuits, main circuit 8bit-Register
module main (
  input  CU,
  input  [7:0] Data_Bus,
  input  Test
);

  wire control_unit_1_enable_mar_write, control_unit_1_mar_read_from_bus, CPU_CLOCK_out;
  wire [3:0] control_unit_1_to_address_bus, INC_sum, MAR_out_3, multiplexer_1_out, multiplexer_3_out,
       PC_out_3;
  wire [7:0] controlled_buffer_1_out, controlled_buffer_3_out, IR_out_2, MBR_out_2, multiplexer_2_out,
       multiplexer_4_out, R1_out_2, R2_out_2, undriven, undriven_2;

  Clock CPU_CLOCK (.out(CPU_CLOCK_out));
  // Probe on PC_out_3
  _4bit_Register PC (.in_1(CPU_CLOCK_out), .in_2(INC_sum), .out_3(PC_out_3));
  // Probe on control_unit_1_to_address_bus
  assign controlled_buffer_1_out = Test ? Data_Bus : 8'bz;  // Controlled_Buffer controlled_buffer_1
  _4_bit_adder INC (.in_1(4'b0001), .in_2(PC_out_3), .Sum(INC_sum));  // open: Overflow
  _8_bit_async_reg R1 (.in_1(controlled_buffer_1_out), .out_2(R1_out_2));
  assign Data_Bus = Test ? R1_out_2 : 8'bz;  // Controlled_Buffer controlled_buffer_2
  Multiplexer #(.width(4), .disabled(0), .enable("false")) multiplexer_1 (
    .in0(PC_out_3), .in1(control_unit_1_to_address_bus), .out(multiplexer_1_out),
    .sel(control_unit_1_mar_read_from_bus));
  assign controlled_buffer_3_out = Test ? Data_Bus : 8'bz;  // Controlled_Buffer controlled_buffer_3
  _8_bit_async_reg R2 (.in_1(controlled_buffer_3_out), .out_2(R2_out_2));
  assign Data_Bus = Test ? R2_out_2 : 8'bz;  // Controlled_Buffer controlled_buffer_4
  _4bit_Register MAR (.in_1(CPU_CLOCK_out), .in_2(multiplexer_1_out), .out_3(MAR_out_3));
  control_unit control_unit_1 (
    .MAR_read_from_bus(control_unit_1_mar_read_from_bus), .Enable_MAR_write(control_unit_1_enable_mar_write),
    .in_1(IR_out_2), .To_Address_Bus(control_unit_1_to_address_bus));
  _8_bit_async_reg MBR (.in_1(multiplexer_2_out), .out_2(MBR_out_2));
  Multiplexer #(.width(8), .disabled(0), .enable("false")) multiplexer_2 (
    .in0(multiplexer_4_out), .in1(undriven), .out(multiplexer_2_out), .sel(CU));
  Multiplexer #(.width(4), .disabled(0)) multiplexer_3 (
    .in0(MAR_out_3), .in1(MAR_out_3), .out(multiplexer_3_out), .sel(CU), .en(control_unit_1_enable_mar_write));
  _8_bit_async_reg IR (.in_1(MBR_out_2), .out_2(IR_out_2));
  Multiplexer #(.width(8), .disabled(0)) multiplexer_4 (
    .in0(undriven_2), .in1(MBR_out_2), .out(multiplexer_4_out), .sel(CU));  // open: en
  // Probe on undriven_2
  RAM RAM (.in_3(multiplexer_3_out));  // open: in_2, in_1, out_4

  // Notes on the sheet:
  //   Data Bus
  //   Address Bus
endmodule

module _8bit_Register (
  input  clock_input,
  input  [7:0] in_2,
  output [7:0] out_3
);

  D_Flip_Flop d_ff_1 (.clk(clock_input), .D(in_2[7]), .Q(out_3[7]));  // open: Qn, preset, en, reset
  D_Flip_Flop d_ff_2 (.clk(clock_input), .D(in_2[6]), .Q(out_3[6]));  // open: Qn, preset, en, reset
  D_Flip_Flop d_ff_3 (.clk(clock_input), .D(in_2[5]), .Q(out_3[5]));  // open: Qn, preset, en, reset
  D_Flip_Flop d_ff_4 (.clk(clock_input), .D(in_2[4]), .Q(out_3[4]));  // open: Qn, preset, en, reset
  D_Flip_Flop d_ff_5 (.clk(clock_input), .D(in_2[3]), .Q(out_3[3]));  // open: Qn, preset, en, reset
  D_Flip_Flop d_ff_6 (.clk(clock_input), .D(in_2[2]), .Q(out_3[2]));  // open: Qn, preset, en, reset
  D_Flip_Flop d_ff_7 (.clk(clock_input), .D(in_2[1]), .Q(out_3[1]));  // open: Qn, preset, en, reset
  D_Flip_Flop d_ff_8 (.clk(clock_input), .D(in_2[0]), .Q(out_3[0]));  // open: Qn, preset, en, reset
endmodule

module _4bit_Register (
  input  in_1,
  input  [3:0] in_2,
  output [3:0] out_3
);

  wire d_ff_1_qn, d_ff_5_qn, undriven, undriven_2, undriven_3, undriven_4, undriven_5, undriven_6;

  D_Flip_Flop d_ff_1 (
    .clk(in_1), .D(in_2[3]), .Q(out_3[3]), .Qn(d_ff_1_qn), .preset(undriven), .en(undriven_2),
    .reset(undriven_3));
  D_Flip_Flop d_ff_2 (.clk(in_1), .D(in_2[2]), .Q(out_3[2]));  // open: Qn, preset, en, reset
  D_Flip_Flop d_ff_3 (
    .clk(in_1), .D(in_2[3]), .Q(out_3[3]), .Qn(d_ff_1_qn), .preset(undriven), .en(undriven_2),
    .reset(undriven_3));
  D_Flip_Flop d_ff_4 (.clk(in_1), .D(in_2[1]), .Q(out_3[1]));  // open: Qn, preset, en, reset
  D_Flip_Flop d_ff_5 (
    .clk(in_1), .D(in_2[0]), .Q(out_3[0]), .Qn(d_ff_5_qn), .preset(undriven_4), .en(undriven_5),
    .reset(undriven_6));
  D_Flip_Flop d_ff_6 (
    .clk(in_1), .D(in_2[0]), .Q(out_3[0]), .Qn(d_ff_5_qn), .preset(undriven_4), .en(undriven_5),
    .reset(undriven_6));
endmodule

module half_adder (
  input  in_1,
  input  in_2,
  output sum_out,
  output carry_out
);

  xor xor_1 (sum_out, in_1, in_2);
  and and_1 (carry_out, in_1, in_2);
endmodule

module full_adder (
  input  in_1,
  input  in_2,
  input  carry,
  output carry_out,
  output sum_out
);

  wire half_adder_2_carry_out, half_adder_carry_out, half_adder_sum_out;

  half_adder half_adder (.in_1(in_1), .in_2(in_2), .sum_out(half_adder_sum_out), .carry_out(half_adder_carry_out));
  half_adder half_adder_2 (
    .in_1(half_adder_sum_out), .in_2(carry), .sum_out(sum_out), .carry_out(half_adder_2_carry_out));
  or or_1 (carry_out, half_adder_carry_out, half_adder_2_carry_out);
endmodule

module _4_bit_adder (
  input  [3:0] in_1,
  input  [3:0] in_2,
  output Overflow,
  output [3:0] Sum
);

  wire full_adder_1_carry_out, full_adder_3_carry_out, half_adder_1_carry_out;

  half_adder half_adder_1 (.in_1(in_1[0]), .in_2(in_2[0]), .sum_out(Sum[0]), .carry_out(half_adder_1_carry_out));
  full_adder full_adder_1 (
    .in_1(in_1[1]), .in_2(in_2[1]), .carry(half_adder_1_carry_out), .carry_out(full_adder_1_carry_out),
    .sum_out(Sum[1]));
  full_adder full_adder_2 (
    .in_1(in_1[3]), .in_2(in_2[3]), .carry(full_adder_3_carry_out), .carry_out(Overflow), .sum_out(Sum[3]));
  full_adder full_adder_3 (
    .in_1(in_1[2]), .in_2(in_2[2]), .carry(full_adder_1_carry_out), .carry_out(full_adder_3_carry_out),
    .sum_out(Sum[2]));
endmodule

module display (
  input  [7:0] in_1
);

  wire addif5_1_out_6, addif5_1_out_7, addif5_1_out_8, addif5_1_out_9, addif5_2_out_6, addif5_2_out_7,
       addif5_2_out_8, addif5_2_out_9, addif5_3_out_6, addif5_3_out_7, addif5_3_out_8, addif5_3_out_9,
       addif5_4_out_6, addif5_4_out_7, addif5_4_out_8, addif5_4_out_9, addif5_5_out_6, addif5_5_out_7,
       addif5_5_out_8, addif5_5_out_9, addif5_6_out_6, addif5_6_out_7, addif5_6_out_8, addif5_6_out_9,
       addif5_7_out_6, addif5_7_out_7, addif5_7_out_8, addif5_7_out_9, n2bitdisplay_1_s1, n2bitdisplay_1_s2,
       n2bitdisplay_1_s3, n2bitdisplay_1_s4, n2bitdisplay_1_s5, n2bitdisplay_1_s6, n2bitdisplay_1_s7,
       n2bitdisplay_1_s8, n4bitdisplay_1_out_5, n4bitdisplay_1_out_6, n4bitdisplay_1_out_7,
       n4bitdisplay_1_out_8, n4bitdisplay_1_out_9, n4bitdisplay_1_out_10, n4bitdisplay_1_out_11,
       n4bitdisplay_1_out_12, n4bitdisplay_2_out_5, n4bitdisplay_2_out_6, n4bitdisplay_2_out_7,
       n4bitdisplay_2_out_8, n4bitdisplay_2_out_9, n4bitdisplay_2_out_10, n4bitdisplay_2_out_11,
       n4bitdisplay_2_out_12;

  _2bitdisplay u_2bitdisplay_1 (
    .a(addif5_1_out_9), .b(addif5_2_out_9), .s1(n2bitdisplay_1_s1), .s2(n2bitdisplay_1_s2),
    .s3(n2bitdisplay_1_s3), .s4(n2bitdisplay_1_s4), .s5(n2bitdisplay_1_s5), .s6(n2bitdisplay_1_s6),
    .s7(n2bitdisplay_1_s7), .s8(n2bitdisplay_1_s8));
  _7_Segment_Display u_7_segment_display_1 (
    .g(n2bitdisplay_1_s1), .f(n2bitdisplay_1_s2), .a(n2bitdisplay_1_s3), .b(n2bitdisplay_1_s4),
    .e(n2bitdisplay_1_s5), .d(n2bitdisplay_1_s6), .c(n2bitdisplay_1_s7), .dp(n2bitdisplay_1_s8));
  addif5 addif5_1 (
    .in_1(addif5_5_out_9), .in_2(addif5_4_out_9), .in_3(addif5_3_out_9), .in_4(1'b0), .out_6(addif5_1_out_6),
    .out_7(addif5_1_out_7), .out_8(addif5_1_out_8), .out_9(addif5_1_out_9));  // open: Overflow
  addif5 addif5_2 (
    .in_1(addif5_6_out_9), .in_2(addif5_1_out_6), .in_3(addif5_1_out_7), .in_4(addif5_1_out_8),
    .out_6(addif5_2_out_6), .out_7(addif5_2_out_7), .out_8(addif5_2_out_8), .out_9(addif5_2_out_9));  // open: Overflow
  addif5 addif5_3 (
    .in_1(in_1[5]), .in_2(in_1[6]), .in_3(in_1[7]), .in_4(1'b0), .out_6(addif5_3_out_6),
    .out_7(addif5_3_out_7), .out_8(addif5_3_out_8), .out_9(addif5_3_out_9));  // open: Overflow
  addif5 addif5_4 (
    .in_1(in_1[4]), .in_2(addif5_3_out_6), .in_3(addif5_3_out_7), .in_4(addif5_3_out_8),
    .out_6(addif5_4_out_6), .out_7(addif5_4_out_7), .out_8(addif5_4_out_8), .out_9(addif5_4_out_9));  // open: Overflow
  addif5 addif5_5 (
    .in_1(in_1[3]), .in_2(addif5_4_out_6), .in_3(addif5_4_out_7), .in_4(addif5_4_out_8),
    .out_6(addif5_5_out_6), .out_7(addif5_5_out_7), .out_8(addif5_5_out_8), .out_9(addif5_5_out_9));  // open: Overflow
  addif5 addif5_6 (
    .in_1(in_1[2]), .in_2(addif5_5_out_6), .in_3(addif5_5_out_7), .in_4(addif5_5_out_8),
    .out_6(addif5_6_out_6), .out_7(addif5_6_out_7), .out_8(addif5_6_out_8), .out_9(addif5_6_out_9));  // open: Overflow
  addif5 addif5_7 (
    .in_1(in_1[1]), .in_2(addif5_6_out_6), .in_3(addif5_6_out_7), .in_4(addif5_6_out_8),
    .out_6(addif5_7_out_6), .out_7(addif5_7_out_7), .out_8(addif5_7_out_8), .out_9(addif5_7_out_9));  // open: Overflow
  _4bitdisplay u_4bitdisplay_1 (
    .a(addif5_2_out_8), .b(addif5_2_out_7), .c(addif5_2_out_6), .d(addif5_7_out_9),
    .out_9(n4bitdisplay_1_out_9), .out_10(n4bitdisplay_1_out_10), .out_11(n4bitdisplay_1_out_11),
    .out_12(n4bitdisplay_1_out_12), .out_5(n4bitdisplay_1_out_5), .out_6(n4bitdisplay_1_out_6),
    .out_7(n4bitdisplay_1_out_7), .out_8(n4bitdisplay_1_out_8));
  _7_Segment_Display u_7_segment_display_2 (
    .g(n4bitdisplay_1_out_5), .f(n4bitdisplay_1_out_6), .a(n4bitdisplay_1_out_7), .b(n4bitdisplay_1_out_8),
    .e(n4bitdisplay_1_out_9), .d(n4bitdisplay_1_out_10), .c(n4bitdisplay_1_out_11), .dp(n4bitdisplay_1_out_12));
  _4bitdisplay u_4bitdisplay_2 (
    .a(addif5_7_out_8), .b(addif5_7_out_7), .c(addif5_7_out_6), .d(in_1[0]), .out_9(n4bitdisplay_2_out_9),
    .out_10(n4bitdisplay_2_out_10), .out_11(n4bitdisplay_2_out_11), .out_12(n4bitdisplay_2_out_12),
    .out_5(n4bitdisplay_2_out_5), .out_6(n4bitdisplay_2_out_6), .out_7(n4bitdisplay_2_out_7),
    .out_8(n4bitdisplay_2_out_8));
  _7_Segment_Display u_7_segment_display_3 (
    .g(n4bitdisplay_2_out_5), .f(n4bitdisplay_2_out_6), .a(n4bitdisplay_2_out_7), .b(n4bitdisplay_2_out_8),
    .e(n4bitdisplay_2_out_9), .d(n4bitdisplay_2_out_10), .c(n4bitdisplay_2_out_11), .dp(n4bitdisplay_2_out_12));

  // Notes on the sheet:
  //   hunds
  //   tens
  //   ones
endmodule

module addif5 (
  input  in_1,
  input  in_2,
  input  in_3,
  input  in_4,
  output Overflow,
  output out_6,
  output out_7,
  output out_8,
  output out_9
);

  wire and_1_out, full_adder_1_carry_out, full_adder_2_carry_out, half_adder_1_carry_out, or_1_out, or_2_out;
  wire [3:0] half_adder_1_sum_out;

  or or_1 (or_1_out, in_2, in_1);
  and and_1 (and_1_out, in_3, or_1_out);
  or or_2 (or_2_out, in_4, and_1_out);
  full_adder full_adder_1 (
    .in_1(1'b1), .in_2(in_2), .carry(half_adder_1_carry_out), .carry_out(full_adder_1_carry_out),
    .sum_out(half_adder_1_sum_out[1]));
  half_adder half_adder_1 (
    .in_1(1'b1), .in_2(in_1), .sum_out(half_adder_1_sum_out[0]), .carry_out(half_adder_1_carry_out));
  Multiplexer #(.width(4), .enable("false")) multiplexer_1 (
    .in0({in_4, in_3, in_2, in_1}), .in1(half_adder_1_sum_out), .out({out_9, out_8, out_7, out_6}),
    .sel(or_2_out));
  full_adder full_adder_2 (
    .in_1(1'b0), .in_2(in_3), .carry(full_adder_1_carry_out), .carry_out(full_adder_2_carry_out),
    .sum_out(half_adder_1_sum_out[2]));
  full_adder full_adder_3 (
    .in_1(1'b0), .in_2(in_4), .carry(full_adder_2_carry_out), .carry_out(Overflow),
    .sum_out(half_adder_1_sum_out[3]));
endmodule

module _4bitdisplay (
  input  a,
  input  b,
  input  c,
  input  d,
  output out_5,
  output out_6,
  output out_7,
  output out_8,
  output out_9,
  output out_10,
  output out_11,
  output out_12
);

  wire and_1_out, and_2_out, and_3_out, and_4_out, and_5_out, and_6_out, and_7_out, and_8_out, and_9_out,
       and_10_out, and_11_out, and_12_out, and_13_out, and_14_out, and_15_out, and_16_out, and_17_out,
       and_18_out, and_19_out, and_20_out, and_21_out, and_22_out, and_23_out, and_24_out, and_25_out,
       and_26_out, not_1_out, not_2_out, not_3_out, not_4_out, not_5_out, not_6_out, not_7_out, not_8_out,
       not_9_out, not_10_out, not_11_out, not_12_out, not_13_out, not_14_out, not_15_out, not_16_out,
       not_17_out, not_18_out, not_19_out, not_20_out, not_21_out, not_22_out, not_23_out, not_24_out,
       not_25_out, not_26_out, not_27_out, not_28_out, not_29_out, not_30_out, not_31_out, not_32_out,
       not_33_out, not_34_out, not_35_out, not_36_out, not_37_out, not_38_out, not_39_out, not_40_out,
       not_41_out, not_42_out, not_43_out, not_44_out, not_45_out, not_46_out, not_47_out, not_48_out,
       not_49_out, not_50_out, not_51_out, not_52_out, not_53_out;

  not not_1 (not_1_out, a);
  and and_1 (and_1_out, not_1_out, not_2_out, c);
  not not_2 (not_2_out, b);
  not not_3 (not_3_out, a);
  and and_2 (and_2_out, not_3_out, b, not_4_out);
  not not_4 (not_4_out, c);
  not not_5 (not_5_out, a);
  and and_3 (and_3_out, not_5_out, b, not_6_out);
  not not_6 (not_6_out, d);
  and and_4 (and_4_out, a, not_7_out, not_8_out);
  not not_7 (not_7_out, b);
  not not_8 (not_8_out, c);
  not not_9 (not_9_out, a);
  and and_5 (and_5_out, not_9_out, not_10_out, not_11_out);
  not not_10 (not_10_out, c);
  not not_11 (not_11_out, d);
  not not_12 (not_12_out, a);
  and and_6 (and_6_out, not_12_out, b, not_13_out);
  not not_13 (not_13_out, c);
  not not_14 (not_14_out, a);
  and and_7 (and_7_out, not_14_out, b, not_15_out);
  not not_15 (not_15_out, d);
  not not_16 (not_16_out, b);
  and and_8 (and_8_out, a, not_16_out, not_17_out);
  not not_17 (not_17_out, c);
  not not_18 (not_18_out, a);
  not not_19 (not_19_out, b);
  and and_9 (and_9_out, not_18_out, not_19_out, not_20_out);
  not not_20 (not_20_out, d);
  not not_21 (not_21_out, a);
  and and_10 (and_10_out, not_21_out, c);
  not not_22 (not_22_out, a);
  and and_11 (and_11_out, not_22_out, b, d);
  and and_12 (and_12_out, a, not_23_out, not_24_out);
  not not_23 (not_23_out, b);
  not not_24 (not_24_out, c);
  not not_25 (not_25_out, a);
  and and_13 (and_13_out, not_25_out, not_26_out);
  not not_26 (not_26_out, b);
  not not_27 (not_27_out, a);
  not not_28 (not_28_out, c);
  and and_14 (and_14_out, not_27_out, not_28_out, not_29_out);
  not not_29 (not_29_out, d);
  not not_30 (not_30_out, b);
  and and_15 (and_15_out, not_30_out, not_31_out);
  not not_31 (not_31_out, c);
  not not_32 (not_32_out, a);
  and and_16 (and_16_out, not_32_out, c, d);
  not not_33 (not_33_out, a);
  not not_34 (not_34_out, b);
  and and_17 (and_17_out, not_33_out, not_34_out, not_35_out);
  not not_35 (not_35_out, d);
  not not_36 (not_36_out, b);
  and and_18 (and_18_out, not_36_out, not_37_out, not_38_out);
  not not_37 (not_37_out, c);
  not not_38 (not_38_out, d);
  not not_39 (not_39_out, a);
  and and_19 (and_19_out, not_39_out, c, not_40_out);
  not not_40 (not_40_out, d);
  not not_41 (not_41_out, b);
  not not_42 (not_42_out, c);
  not not_43 (not_43_out, d);
  not not_44 (not_44_out, a);
  not not_45 (not_45_out, b);
  not not_46 (not_46_out, a);
  not not_47 (not_47_out, d);
  not not_48 (not_48_out, a);
  not not_49 (not_49_out, c);
  not not_50 (not_50_out, b);
  and and_20 (and_20_out, not_50_out, not_51_out);
  not not_51 (not_51_out, c);
  not not_52 (not_52_out, a);
  and and_21 (and_21_out, not_52_out, d);
  not not_53 (not_53_out, a);
  and and_22 (and_22_out, not_53_out, b);
  or or_1 (out_5, and_1_out, and_2_out, and_3_out, and_4_out);
  or or_2 (out_6, and_5_out, and_6_out, and_7_out, and_8_out);
  or or_3 (out_7, and_9_out, and_10_out, and_11_out, and_12_out);
  or or_4 (out_8, and_13_out, and_14_out, and_15_out, and_16_out);
  or or_5 (out_9, and_17_out, and_18_out, and_19_out);
  and and_23 (and_23_out, not_41_out, not_42_out, not_43_out);
  and and_24 (and_24_out, not_44_out, not_45_out, c);
  and and_25 (and_25_out, not_46_out, c, not_47_out);
  and and_26 (and_26_out, not_48_out, b, not_49_out, d);
  or or_6 (out_11, and_20_out, and_21_out, and_22_out);
  or or_7 (out_10, and_23_out, and_24_out, and_25_out, and_26_out);

  assign out_12 = 1'b0;
endmodule

module _2bitdisplay (
  input  a,
  input  b,
  output s1,
  output s2,
  output s3,
  output s4,
  output s5,
  output s6,
  output s7,
  output s8
);

  wire not_1_out, not_2_out, not_3_out, not_5_out, not_6_out;

  not not_1 (not_1_out, b);
  not not_2 (not_2_out, a);
  not not_3 (not_3_out, b);
  not not_4 (s3, b);
  not not_5 (not_5_out, a);
  not not_6 (not_6_out, b);
  not not_7 (s5, b);
  not not_8 (s6, b);
  not not_9 (s7, a);
  and and_1 (s1, a, not_1_out);
  and and_2 (s2, not_2_out, not_3_out);
  or or_1 (s4, not_5_out, not_6_out);

  assign s8 = 1'b0;
endmodule

module RAM (
  input  [7:0] in_1,
  input  in_2,
  input  [3:0] in_3,
  output [7:0] out_4
);

  wire Mode_Register_out_2;
  wire [3:0] Address_Register_out_2;
  wire [7:0] demultiplexer_1_out0, demultiplexer_1_out1, demultiplexer_1_out2, demultiplexer_1_out3,
       demultiplexer_1_out4, demultiplexer_1_out5, demultiplexer_1_out6, demultiplexer_1_out7,
       demultiplexer_1_out8, demultiplexer_1_out9, demultiplexer_1_out10, demultiplexer_1_out11,
       demultiplexer_1_out12, demultiplexer_1_out13, demultiplexer_1_out14, demultiplexer_1_out15,
       multiplexer_1_out, multiplexer_2_out, n8_bit_async_reg_1_out_2, n8_bit_async_reg_2_out_2,
       n8_bit_async_reg_3_out_2, n8_bit_async_reg_4_out_2, n8_bit_async_reg_5_out_2,
       n8_bit_async_reg_6_out_2, n8_bit_async_reg_7_out_2, n8_bit_async_reg_8_out_2,
       n8_bit_async_reg_9_out_2, n8_bit_async_reg_10_out_2, n8_bit_async_reg_11_out_2,
       n8_bit_async_reg_12_out_2, n8_bit_async_reg_13_out_2, n8_bit_async_reg_14_out_2,
       n8_bit_async_reg_15_out_2, n8_bit_async_reg_16_out_2;

  Demultiplexer #(.select(4), .width(8), .tristate("true")) demultiplexer_1 (
    .out0(demultiplexer_1_out0), .out1(demultiplexer_1_out1), .out2(demultiplexer_1_out2),
    .out3(demultiplexer_1_out3), .out4(demultiplexer_1_out4), .out5(demultiplexer_1_out5),
    .out6(demultiplexer_1_out6), .out7(demultiplexer_1_out7), .out8(demultiplexer_1_out8),
    .out9(demultiplexer_1_out9), .out10(demultiplexer_1_out10), .out11(demultiplexer_1_out11),
    .out12(demultiplexer_1_out12), .out13(demultiplexer_1_out13), .out14(demultiplexer_1_out14),
    .out15(demultiplexer_1_out15), .in(out_4), .sel(Address_Register_out_2), .en(Mode_Register_out_2));
  _8_bit_async_reg u_8_bit_async_reg_1 (.in_1(demultiplexer_1_out0), .out_2(n8_bit_async_reg_1_out_2));
  _8_bit_async_reg u_8_bit_async_reg_2 (.in_1(demultiplexer_1_out1), .out_2(n8_bit_async_reg_2_out_2));
  _8_bit_async_reg u_8_bit_async_reg_3 (.in_1(demultiplexer_1_out2), .out_2(n8_bit_async_reg_3_out_2));
  _8_bit_async_reg u_8_bit_async_reg_4 (.in_1(demultiplexer_1_out3), .out_2(n8_bit_async_reg_4_out_2));
  _8_bit_async_reg u_8_bit_async_reg_5 (.in_1(demultiplexer_1_out4), .out_2(n8_bit_async_reg_5_out_2));
  _8_bit_async_reg u_8_bit_async_reg_6 (.in_1(demultiplexer_1_out5), .out_2(n8_bit_async_reg_6_out_2));
  _8_bit_async_reg u_8_bit_async_reg_7 (.in_1(demultiplexer_1_out6), .out_2(n8_bit_async_reg_7_out_2));
  _8_bit_async_reg u_8_bit_async_reg_8 (.in_1(demultiplexer_1_out7), .out_2(n8_bit_async_reg_8_out_2));
  _8_bit_async_reg u_8_bit_async_reg_9 (.in_1(demultiplexer_1_out8), .out_2(n8_bit_async_reg_9_out_2));
  _8_bit_async_reg u_8_bit_async_reg_10 (.in_1(demultiplexer_1_out9), .out_2(n8_bit_async_reg_10_out_2));
  _8_bit_async_reg u_8_bit_async_reg_11 (.in_1(demultiplexer_1_out10), .out_2(n8_bit_async_reg_11_out_2));
  _8_bit_async_reg u_8_bit_async_reg_12 (.in_1(demultiplexer_1_out11), .out_2(n8_bit_async_reg_12_out_2));
  _8_bit_async_reg u_8_bit_async_reg_13 (.in_1(demultiplexer_1_out12), .out_2(n8_bit_async_reg_13_out_2));
  _8_bit_async_reg u_8_bit_async_reg_14 (.in_1(demultiplexer_1_out13), .out_2(n8_bit_async_reg_14_out_2));
  _8_bit_async_reg u_8_bit_async_reg_15 (.in_1(demultiplexer_1_out14), .out_2(n8_bit_async_reg_15_out_2));
  _8_bit_async_reg u_8_bit_async_reg_16 (.in_1(demultiplexer_1_out15), .out_2(n8_bit_async_reg_16_out_2));
  _1_bit_async_register Mode_Register (.in_1(in_2), .out_2(Mode_Register_out_2));
  Multiplexer #(.select(4), .width(8), .disabled(0), .enable("false")) multiplexer_1 (
    .in0(n8_bit_async_reg_1_out_2), .in1(n8_bit_async_reg_2_out_2), .in2(n8_bit_async_reg_3_out_2),
    .in3(n8_bit_async_reg_4_out_2), .in4(n8_bit_async_reg_5_out_2), .in5(n8_bit_async_reg_6_out_2),
    .in6(n8_bit_async_reg_7_out_2), .in7(n8_bit_async_reg_8_out_2), .in8(n8_bit_async_reg_9_out_2),
    .in9(n8_bit_async_reg_10_out_2), .in10(n8_bit_async_reg_11_out_2), .in11(n8_bit_async_reg_12_out_2),
    .in12(n8_bit_async_reg_13_out_2), .in13(n8_bit_async_reg_14_out_2), .in14(n8_bit_async_reg_15_out_2),
    .in15(n8_bit_async_reg_16_out_2), .out(multiplexer_1_out), .sel(Address_Register_out_2));
  _4_bit_async_reg Address_Register (.in_1(in_3), .out_2(Address_Register_out_2));
  Multiplexer #(.width(8), .disabled(0), .enable("false")) multiplexer_2 (
    .in0(multiplexer_1_out), .in1(in_1), .out(multiplexer_2_out), .sel(Mode_Register_out_2));
  _8_bit_async_reg Data_Register (.in_1(multiplexer_2_out), .out_2(out_4));
endmodule

module _8_bit_async_reg (
  input  [7:0] in_1,
  output [7:0] out_2
);

  D_Flip_Flop #(.trigger("high")) d_ff_1 (.clk(1'b1), .D(in_1[6]), .Q(out_2[6]));  // open: Qn, preset, en, reset
  D_Flip_Flop #(.trigger("high")) d_ff_2 (.clk(1'b1), .D(in_1[7]), .Q(out_2[7]));  // open: Qn, preset, en, reset
  D_Flip_Flop #(.trigger("high")) d_ff_3 (.clk(1'b1), .D(in_1[5]), .Q(out_2[5]));  // open: Qn, preset, en, reset
  D_Flip_Flop #(.trigger("high")) d_ff_4 (.clk(1'b1), .D(in_1[4]), .Q(out_2[4]));  // open: Qn, preset, en, reset
  D_Flip_Flop #(.trigger("high")) d_ff_5 (.clk(1'b1), .D(in_1[3]), .Q(out_2[3]));  // open: Qn, preset, en, reset
  D_Flip_Flop #(.trigger("high")) d_ff_6 (.clk(1'b1), .D(in_1[2]), .Q(out_2[2]));  // open: Qn, preset, en, reset
  D_Flip_Flop #(.trigger("high")) d_ff_7 (.clk(1'b1), .D(in_1[1]), .Q(out_2[1]));  // open: Qn, preset, en, reset
  D_Flip_Flop #(.trigger("high")) d_ff_8 (.clk(1'b1), .D(in_1[0]), .Q(out_2[0]));  // open: Qn, preset, en, reset
endmodule

module _4_bit_async_reg (
  input  [3:0] in_1,
  output [3:0] out_2
);

  wire d_ff_2_qn, d_ff_5_qn, undriven, undriven_2, undriven_3, undriven_4, undriven_5, undriven_6;

  D_Flip_Flop #(.trigger("high")) d_ff_1 (.clk(1'b1), .D(in_1[2]), .Q(out_2[2]));  // open: Qn, preset, en, reset
  D_Flip_Flop #(.trigger("high")) d_ff_2 (
    .clk(1'b1), .D(in_1[3]), .Q(out_2[3]), .Qn(d_ff_2_qn), .preset(undriven), .en(undriven_2),
    .reset(undriven_3));
  D_Flip_Flop #(.trigger("high")) d_ff_3 (
    .clk(1'b1), .D(in_1[3]), .Q(out_2[3]), .Qn(d_ff_2_qn), .preset(undriven), .en(undriven_2),
    .reset(undriven_3));
  D_Flip_Flop #(.trigger("high")) d_ff_4 (.clk(1'b1), .D(in_1[1]), .Q(out_2[1]));  // open: Qn, preset, en, reset
  D_Flip_Flop #(.trigger("high")) d_ff_5 (
    .clk(1'b1), .D(in_1[0]), .Q(out_2[0]), .Qn(d_ff_5_qn), .preset(undriven_4), .en(undriven_5),
    .reset(undriven_6));
  D_Flip_Flop #(.trigger("high")) d_ff_6 (
    .clk(1'b1), .D(in_1[0]), .Q(out_2[0]), .Qn(d_ff_5_qn), .preset(undriven_4), .en(undriven_5),
    .reset(undriven_6));
endmodule

module control_unit (
  input  [7:0] in_1,
  output MAR_read_from_bus,
  output Enable_MAR_write,
  output [3:0] To_Address_Bus
);

  assign To_Address_Bus = Enable_MAR_write ? in_1[3:0] : 4'bz;  // Controlled_Buffer controlled_buffer_1
  Decoder #(.select(2), .enable("false")) decoder_1 (
    .out0(Enable_MAR_write), .sel(in_1[7:6]));  // open: out1, out2, out3

  assign MAR_read_from_bus = Enable_MAR_write;
endmodule

module inputbuffer (
  input  _0,
  input  _1,
  input  _2,
  input  _3,
  input  _4,
  input  _5,
  input  _6,
  input  _7,
  input  _8,
  input  _9,
  output [7:0] out_11
);

  wire [7:0] multiplexer_1_out, multiplexer_2_out, multiplexer_3_out, multiplexer_4_out, multiplexer_5_out,
       multiplexer_6_out, multiplexer_7_out, multiplexer_8_out, multiplexer_9_out, multiplexer_10_out,
       or_1_out;

  Multiplexer #(.width(8), .disabled(0), .enable("false")) multiplexer_1 (
    .in0({8{1'b0}}), .in1({8{1'b0}}), .out(multiplexer_1_out), .sel(_0));
  Multiplexer #(.width(8), .disabled(0), .enable("false")) multiplexer_2 (
    .in0({8{1'b0}}), .in1(8'h1), .out(multiplexer_2_out), .sel(_1));
  Multiplexer #(.width(8), .disabled(0), .enable("false")) multiplexer_3 (
    .in0({8{1'b0}}), .in1(8'h2), .out(multiplexer_3_out), .sel(_2));
  Multiplexer #(.width(8), .disabled(0), .enable("false")) multiplexer_4 (
    .in0({8{1'b0}}), .in1(8'h3), .out(multiplexer_4_out), .sel(_3));
  Multiplexer #(.width(8), .disabled(0), .enable("false")) multiplexer_5 (
    .in0({8{1'b0}}), .in1(8'h4), .out(multiplexer_5_out), .sel(_4));
  Multiplexer #(.width(8), .disabled(0), .enable("false")) multiplexer_6 (
    .in0({8{1'b0}}), .in1(8'h5), .out(multiplexer_6_out), .sel(_5));
  Multiplexer #(.width(8), .disabled(0), .enable("false")) multiplexer_7 (
    .in0({8{1'b0}}), .in1(8'h6), .out(multiplexer_7_out), .sel(_6));
  Multiplexer #(.width(8), .disabled(0), .enable("false")) multiplexer_8 (
    .in0({8{1'b0}}), .in1(8'h7), .out(multiplexer_8_out), .sel(_7));
  Multiplexer #(.width(8), .disabled(0), .enable("false")) multiplexer_9 (
    .in0({8{1'b0}}), .in1(8'h8), .out(multiplexer_9_out), .sel(_8));
  Multiplexer #(.width(8), .disabled(0), .enable("false")) multiplexer_10 (
    .in0({8{1'b0}}), .in1(8'h9), .out(multiplexer_10_out), .sel(_9));
  assign or_1_out = multiplexer_1_out | multiplexer_2_out | multiplexer_3_out | multiplexer_4_out | multiplexer_5_out | multiplexer_6_out | multiplexer_7_out | multiplexer_8_out | multiplexer_9_out | multiplexer_10_out;  // OR_Gate or_1, 8 bits wide
  _8_bit_async_reg u_8_bit_async_reg_1 (.in_1(or_1_out), .out_2(out_11));
endmodule

module _1_bit_async_register (
  input  in_1,
  output out_2
);

  wire d_ff_1_qn, undriven, undriven_2, undriven_3;

  D_Flip_Flop #(.trigger("high")) d_ff_1 (
    .clk(1'b1), .D(in_1), .Q(out_2), .Qn(d_ff_1_qn), .preset(undriven), .en(undriven_2), .reset(undriven_3));
  D_Flip_Flop #(.trigger("high")) d_ff_2 (
    .clk(1'b1), .D(in_1), .Q(out_2), .Qn(d_ff_1_qn), .preset(undriven), .en(undriven_2), .reset(undriven_3));
endmodule

module _8_bit_adder (
  input  [7:0] in_1,
  input  [7:0] in_2,
  output out_3,
  output [7:0] out_4
);

  wire full_adder_1_carry_out, full_adder_2_carry_out, full_adder_3_carry_out, full_adder_4_carry_out,
       full_adder_5_carry_out, full_adder_6_carry_out, half_adder_1_carry_out;
  wire [7:0] n8_bit_async_reg_1_out_2, n8_bit_async_reg_2_out_2;

  _8_bit_async_reg u_8_bit_async_reg_1 (.in_1(in_1), .out_2(n8_bit_async_reg_1_out_2));
  _8_bit_async_reg u_8_bit_async_reg_2 (.in_1(in_2), .out_2(n8_bit_async_reg_2_out_2));
  full_adder full_adder_1 (
    .in_1(n8_bit_async_reg_1_out_2[4]), .in_2(n8_bit_async_reg_2_out_2[4]), .carry(full_adder_2_carry_out),
    .carry_out(full_adder_1_carry_out), .sum_out(out_4[4]));
  full_adder full_adder_2 (
    .in_1(n8_bit_async_reg_1_out_2[3]), .in_2(n8_bit_async_reg_2_out_2[3]), .carry(full_adder_3_carry_out),
    .carry_out(full_adder_2_carry_out), .sum_out(out_4[3]));
  full_adder full_adder_3 (
    .in_1(n8_bit_async_reg_1_out_2[2]), .in_2(n8_bit_async_reg_2_out_2[2]), .carry(full_adder_4_carry_out),
    .carry_out(full_adder_3_carry_out), .sum_out(out_4[2]));
  full_adder full_adder_4 (
    .in_1(n8_bit_async_reg_1_out_2[1]), .in_2(n8_bit_async_reg_2_out_2[1]), .carry(half_adder_1_carry_out),
    .carry_out(full_adder_4_carry_out), .sum_out(out_4[1]));
  half_adder half_adder_1 (
    .in_1(n8_bit_async_reg_1_out_2[0]), .in_2(n8_bit_async_reg_2_out_2[0]), .sum_out(out_4[0]),
    .carry_out(half_adder_1_carry_out));
  full_adder full_adder_5 (
    .in_1(n8_bit_async_reg_1_out_2[6]), .in_2(n8_bit_async_reg_2_out_2[6]), .carry(full_adder_6_carry_out),
    .carry_out(full_adder_5_carry_out), .sum_out(out_4[6]));
  full_adder full_adder_6 (
    .in_1(n8_bit_async_reg_1_out_2[5]), .in_2(n8_bit_async_reg_2_out_2[5]), .carry(full_adder_1_carry_out),
    .carry_out(full_adder_6_carry_out), .sum_out(out_4[5]));
  full_adder full_adder_7 (
    .in_1(n8_bit_async_reg_1_out_2[7]), .in_2(n8_bit_async_reg_2_out_2[7]), .carry(full_adder_5_carry_out),
    .carry_out(out_3), .sum_out(out_4[7]));
endmodule

module multiply (
  input  [7:0] in_1,
  input  in_2,
  output [7:0] out_3
);

  wire and_1_out, and_2_out, and_3_out, and_4_out, and_5_out, and_6_out, and_7_out, and_8_out, and_9_out,
       and_10_out, and_11_out, and_12_out, and_13_out, and_14_out, and_15_out, and_16_out, and_17_out,
       and_18_out, and_19_out, and_20_out, and_21_out, and_22_out, and_23_out, and_24_out, and_25_out,
       and_26_out, and_27_out, and_28_out, and_29_out, and_30_out, and_31_out, and_32_out, and_33_out,
       and_34_out, and_35_out, and_36_out, and_37_out, and_38_out, and_39_out, and_40_out, j_k_ff_1_q,
       j_k_ff_1_qn, j_k_ff_17_qn, not_1_out, not_2_out, not_3_out, not_4_out, not_5_out, not_6_out,
       not_7_out, not_8_out, not_9_out, not_10_out, not_11_out, not_12_out, not_13_out, not_14_out,
       not_15_out, not_16_out, not_17_out, or_1_out, or_2_out, or_3_out, or_4_out, or_5_out, or_6_out,
       or_7_out, or_8_out, or_9_out, or_10_out, or_11_out, or_12_out, or_13_out, or_14_out, or_15_out,
       or_16_out;
  wire [7:0] j_k_ff_16_q, n8_bit_adder_1_out_4, n8_bit_async_reg_1_out_2;

  J_K_Flip_Flop j_k_ff_1 (
    .J(in_2), .clk(in_2), .K(not_1_out), .Q(j_k_ff_1_q), .Qn(j_k_ff_1_qn));  // open: preset, en, reset
  not not_1 (not_1_out, in_2);
  _8_bit_async_reg u_8_bit_async_reg_1 (.in_1(in_1), .out_2(n8_bit_async_reg_1_out_2));
  and and_1 (and_1_out, n8_bit_adder_1_out_4[7], j_k_ff_1_qn, out_3[0]);
  and and_2 (and_2_out, 1'b0, j_k_ff_1_q);
  not not_2 (not_2_out, or_1_out);
  and and_3 (and_3_out, j_k_ff_1_qn, j_k_ff_17_qn, j_k_ff_16_q[7]);
  and and_4 (and_4_out, j_k_ff_16_q[0], j_k_ff_1_q);
  and and_5 (and_5_out, j_k_ff_1_qn, out_3[7]);
  or or_1 (or_1_out, and_1_out, and_3_out, and_2_out);
  J_K_Flip_Flop j_k_ff_2 (.J(or_1_out), .clk(in_2), .K(not_2_out), .Q(j_k_ff_16_q[7]));  // open: Qn, preset, en, reset
  or or_2 (or_2_out, and_5_out, and_4_out);
  J_K_Flip_Flop j_k_ff_3 (.J(or_2_out), .clk(in_2), .K(not_3_out), .Q(out_3[7]));  // open: Qn, preset, en, reset
  not not_3 (not_3_out, or_2_out);
  and and_6 (and_6_out, n8_bit_adder_1_out_4[6], j_k_ff_1_qn, out_3[0]);
  and and_7 (and_7_out, j_k_ff_16_q[7], j_k_ff_1_q);
  and and_8 (and_8_out, j_k_ff_1_qn, j_k_ff_17_qn, j_k_ff_16_q[6]);
  and and_9 (and_9_out, out_3[7], j_k_ff_1_q);
  and and_10 (and_10_out, j_k_ff_1_qn, out_3[6]);
  _8_bit_adder u_8_bit_adder_1 (
    .in_1(n8_bit_async_reg_1_out_2), .in_2(j_k_ff_16_q), .out_4(n8_bit_adder_1_out_4));  // open: out_3
  or or_3 (or_3_out, and_6_out, and_8_out, and_7_out);
  J_K_Flip_Flop j_k_ff_4 (.J(or_3_out), .clk(in_2), .K(not_4_out), .Q(j_k_ff_16_q[6]));  // open: Qn, preset, en, reset
  not not_4 (not_4_out, or_3_out);
  or or_4 (or_4_out, and_10_out, and_9_out);
  J_K_Flip_Flop j_k_ff_5 (.J(or_4_out), .clk(in_2), .K(not_5_out), .Q(out_3[6]));  // open: Qn, preset, en, reset
  not not_5 (not_5_out, or_4_out);
  and and_11 (and_11_out, n8_bit_adder_1_out_4[5], j_k_ff_1_qn, out_3[0]);
  and and_12 (and_12_out, j_k_ff_16_q[6], j_k_ff_1_q);
  and and_13 (and_13_out, j_k_ff_1_qn, j_k_ff_17_qn, j_k_ff_16_q[5]);
  and and_14 (and_14_out, out_3[6], j_k_ff_1_q);
  and and_15 (and_15_out, j_k_ff_1_qn, out_3[5]);
  or or_5 (or_5_out, and_11_out, and_13_out, and_12_out);
  J_K_Flip_Flop j_k_ff_6 (.J(or_5_out), .clk(in_2), .K(not_6_out), .Q(j_k_ff_16_q[5]));  // open: Qn, preset, en, reset
  not not_6 (not_6_out, or_5_out);
  or or_6 (or_6_out, and_15_out, and_14_out);
  J_K_Flip_Flop j_k_ff_7 (.J(or_6_out), .clk(in_2), .K(not_7_out), .Q(out_3[5]));  // open: Qn, preset, en, reset
  not not_7 (not_7_out, or_6_out);
  and and_16 (and_16_out, n8_bit_adder_1_out_4[4], j_k_ff_1_qn, out_3[0]);
  and and_17 (and_17_out, j_k_ff_16_q[5], j_k_ff_1_q);
  and and_18 (and_18_out, j_k_ff_1_qn, j_k_ff_17_qn, j_k_ff_16_q[4]);
  and and_19 (and_19_out, out_3[5], j_k_ff_1_q);
  and and_20 (and_20_out, j_k_ff_1_qn, out_3[4]);
  or or_7 (or_7_out, and_16_out, and_18_out, and_17_out);
  J_K_Flip_Flop j_k_ff_8 (.J(or_7_out), .clk(in_2), .K(not_8_out), .Q(j_k_ff_16_q[4]));  // open: Qn, preset, en, reset
  not not_8 (not_8_out, or_7_out);
  or or_8 (or_8_out, and_20_out, and_19_out);
  not not_9 (not_9_out, or_8_out);
  and and_21 (and_21_out, j_k_ff_16_q[4], j_k_ff_1_q);
  and and_22 (and_22_out, j_k_ff_1_qn, j_k_ff_17_qn, j_k_ff_16_q[3]);
  and and_23 (and_23_out, out_3[4], j_k_ff_1_q);
  J_K_Flip_Flop j_k_ff_9 (.J(or_8_out), .clk(in_2), .K(not_9_out), .Q(out_3[4]));  // open: Qn, preset, en, reset
  and and_24 (and_24_out, j_k_ff_1_qn, out_3[3]);
  and and_25 (and_25_out, n8_bit_adder_1_out_4[3], j_k_ff_1_qn, out_3[0]);
  or or_9 (or_9_out, and_25_out, and_22_out, and_21_out);
  not not_10 (not_10_out, or_9_out);
  or or_10 (or_10_out, and_24_out, and_23_out);
  not not_11 (not_11_out, or_10_out);
  and and_26 (and_26_out, j_k_ff_16_q[3], j_k_ff_1_q);
  J_K_Flip_Flop j_k_ff_10 (
    .J(or_9_out), .clk(in_2), .K(not_10_out), .Q(j_k_ff_16_q[3]));  // open: Qn, preset, en, reset
  and and_27 (and_27_out, j_k_ff_1_qn, j_k_ff_17_qn, j_k_ff_16_q[2]);
  and and_28 (and_28_out, out_3[3], j_k_ff_1_q);
  J_K_Flip_Flop j_k_ff_11 (.J(or_10_out), .clk(in_2), .K(not_11_out), .Q(out_3[3]));  // open: Qn, preset, en, reset
  and and_29 (and_29_out, j_k_ff_1_qn, out_3[2]);
  and and_30 (and_30_out, n8_bit_adder_1_out_4[2], j_k_ff_1_qn, out_3[0]);
  or or_11 (or_11_out, and_30_out, and_27_out, and_26_out);
  not not_12 (not_12_out, or_11_out);
  not not_13 (not_13_out, or_12_out);
  and and_31 (and_31_out, j_k_ff_16_q[2], j_k_ff_1_q);
  J_K_Flip_Flop j_k_ff_12 (
    .J(or_11_out), .clk(in_2), .K(not_12_out), .Q(j_k_ff_16_q[2]));  // open: Qn, preset, en, reset
  and and_32 (and_32_out, j_k_ff_1_qn, j_k_ff_17_qn, j_k_ff_16_q[1]);
  or or_12 (or_12_out, and_29_out, and_28_out);
  and and_33 (and_33_out, out_3[2], j_k_ff_1_q);
  J_K_Flip_Flop j_k_ff_13 (.J(or_12_out), .clk(in_2), .K(not_13_out), .Q(out_3[2]));  // open: Qn, preset, en, reset
  and and_34 (and_34_out, j_k_ff_1_qn, out_3[1]);
  and and_35 (and_35_out, n8_bit_adder_1_out_4[1], j_k_ff_1_qn, out_3[0]);
  not not_14 (not_14_out, or_13_out);
  not not_15 (not_15_out, or_14_out);
  or or_13 (or_13_out, and_35_out, and_32_out, and_31_out);
  and and_36 (and_36_out, j_k_ff_16_q[1], j_k_ff_1_q);
  J_K_Flip_Flop j_k_ff_14 (
    .J(or_13_out), .clk(in_2), .K(not_14_out), .Q(j_k_ff_16_q[1]));  // open: Qn, preset, en, reset
  and and_37 (and_37_out, j_k_ff_1_qn, j_k_ff_17_qn, j_k_ff_16_q[0]);
  or or_14 (or_14_out, and_34_out, and_33_out);
  J_K_Flip_Flop j_k_ff_15 (.J(or_14_out), .clk(in_2), .K(not_15_out), .Q(out_3[1]));  // open: Qn, preset, en, reset
  and and_38 (and_38_out, n8_bit_adder_1_out_4[0], j_k_ff_1_qn, out_3[0]);
  not not_16 (not_16_out, or_15_out);
  and and_39 (and_39_out, out_3[1], j_k_ff_1_q);
  not not_17 (not_17_out, or_16_out);
  and and_40 (and_40_out, j_k_ff_1_qn, out_3[0]);
  or or_15 (or_15_out, and_38_out, and_37_out, and_36_out);
  J_K_Flip_Flop j_k_ff_16 (
    .J(or_15_out), .clk(in_2), .K(not_16_out), .Q(j_k_ff_16_q[0]));  // open: Qn, preset, en, reset
  or or_16 (or_16_out, and_40_out, and_39_out);
  J_K_Flip_Flop j_k_ff_17 (
    .J(or_16_out), .clk(in_2), .K(not_17_out), .Q(out_3[0]), .Qn(j_k_ff_17_qn));  // open: preset, en, reset

  // Notes on the sheet:
  //   shift
  //   Register
endmodule
